# Fritzing sketch boarduino (saved by Fritzing 0.9.0b)
breadboards: 1

parts:
  V1 = DC Power [voltage=5]  # not connected
  U2 = atmega328 [package=dip]
  R4 = Resistor [tolerance=±5% resistance=220 package=THT]
  R5 = Resistor [tolerance=±5% resistance=220 package=THT]
  S4 = Pushbutton [package="[SMD]"]
  R6 = Resistor [tolerance=±5% resistance=10k package=THT]
  LED3 = LED - 5mm [color="Red (633nm)" package="5 mm [THT]"]
  C4 = Electrolytic Capacitor [capacitance=10µF package="100 mil [THT, electrolytic]"]
  XTAL2 = Crystal [frequency="16 Mhz" package=THT]
  LED4 = LED - 5mm [color="Yellow (595nm)" package="5 mm [THT]"]
  C5 = Ceramic Capacitor [capacitance="100 nF" package="1206 [SMD, multilayer]"]
  C6 = Ceramic Capacitor [capacitance="100 nF" package="1206 [SMD, multilayer]"]

nets:
  N1: U2.RESET, S4.Pin_1, S4.Pin_2, R6.Pin_0
  N2: U2.VCC, U2.AVCC, R4.Pin_1, R6.Pin_1, C4.+
  N3: U2.GND, S4.Pin_3, S4.Pin_4, LED3.cathode, C4.-, LED4.cathode, C5.1, C6.0
  N4: U2.XLAT1, XTAL2.pin_0, C6.1
  N5: U2.XLAT2, XTAL2.pin_1, C5.0
  N6: U2.D13, R5.Pin_0
  N7: R4.Pin_0, LED3.anode
  N8: R5.Pin_1, LED4.anode
