# Fritzing sketch ledmatrix (saved by Fritzing 0.9.0b)
circuit board: 8.46667cm x 5.64444cm
breadboards: 1

parts:
  R1 = Resistor [tolerance=±5% resistance=220 package=THT]
  LED1 = LED - 5mm [color="Red (633nm)" package="5 mm [THT]"]
  V1 = DC Power [voltage=5]  # not connected
  U1 = atmega328 [package=dip]
  S3 = Pushbutton [package="[SMD]"]
  R2 = Resistor [tolerance=±5% resistance=10k package=THT]
  C1 = Electrolytic Capacitor [capacitance=10µF package="100 mil [THT, electrolytic]"]
  XTAL1 = Crystal [frequency="16 Mhz" package=THT]
  LED2 = LED - 5mm [color="Yellow (595nm)" package="5 mm [THT]"]
  C2 = Ceramic Capacitor [capacitance="100 nF" package="1206 [SMD, multilayer]"]
  C3 = Ceramic Capacitor [capacitance="100 nF" package="1206 [SMD, multilayer]"]
  R3 = Resistor [tolerance=±5% resistance=220 package=THT]
  U2 = 74HC595 [package="DIP16 [THT]"]
  U3 = 74HC595 [package="DIP16 [THT]"]
  R4 = Resistor [tolerance=±5% resistance=250 package=THT]
  R5 = Resistor [tolerance=±5% resistance=250 package=THT]
  R6 = Resistor [tolerance=±5% resistance=250 package=THT]
  R7 = Resistor [tolerance=±5% resistance=250 package=THT]
  R8 = Resistor [tolerance=±5% resistance=250 package=THT]
  R9 = Resistor [tolerance=±5% resistance=250 package=THT]
  R10 = Resistor [tolerance=±5% resistance=250 package=THT]
  R11 = Resistor [tolerance=±5% resistance=250 package=THT]
  U4 = mystery part, 24 pins [chip_label=?]
  U4_2 = mystery part, 24 pins [chip_label=?]

nets (from the breadboard view):
  N1: R1.Pin_0, LED1.anode
  VCC: R1.Pin_1, U1.VCC, U1.AVCC, S3.Pin_3, S3.Pin_4, R2.Pin_1, C1.+, U2.VCC, U3.VCC
  GND: LED1.cathode, U1.GND, C1.-, LED2.cathode, C2.1, C3.0, U2.GND, U3.GND
  N2: U1.RESET, S3.Pin_1, S3.Pin_2, R2.Pin_0
  N3: U1.XLAT1, XTAL1.pin_0, C3.1
  N4: U1.XLAT2, XTAL1.pin_1, C2.0
  N5: U1.D9_(PWM), U2.ST_CP, U3.ST_CP
  N6: U1.D10_(PWM), U2.SH_CP, U3.SH_CP
  N7: U1.D11_(PWM), U2.DS
  N8: U1.D13, R3.Pin_1
  N9: LED2.anode, R3.Pin_0
  N10: U2.Q1, R5.Pin_1
  N11: U2.Q2, R6.Pin_1
  N12: U2.Q3, R7.Pin_1
  N13: U2.Q4, R8.Pin_1
  N14: U2.Q5, R11.Pin_1
  N15: U2.Q6, R9.Pin_1
  N16: U2.Q7, R10.Pin_1
  N17: U2.Q7', U3.DS
  N18: U2.Q0, R4.Pin_0
  N19: U3.Q1, U4.pin21, U4_2.pin21
  N20: U3.Q2, U4.pin18, U4_2.pin18
  N21: U3.Q3, U4.pin15, U4_2.pin15
  N22: U3.Q4, U4.pin1, U4_2.pin1
  N23: U3.Q5, U4.pin4, U4_2.pin4
  N24: U3.Q6, U4.pin7, U4_2.pin7
  N25: U3.Q7, U4.pin10, U4_2.pin10
  N26: U3.Q0, U4.pin24, U4_2.pin24
  N27: R4.Pin_1, U4.pin22, U4_2.pin22
  N28: R5.Pin_0, U4.pin19, U4_2.pin19
  N29: R6.Pin_0, U4.pin16, U4_2.pin16
  N30: R7.Pin_0, U4.pin13, U4_2.pin13
  N31: R8.Pin_0, U4.pin3, U4_2.pin3
  N32: R9.Pin_0, U4.pin9, U4_2.pin9
  N33: R10.Pin_0, U4.pin12, U4_2.pin12
  N34: R11.Pin_0, U4.pin6, U4_2.pin6
  N35: U4.pin2, U4_2.pin2
  N36: U4.pin5, U4_2.pin5
  N37: U4.pin8, U4_2.pin8
  N38: U4.pin11, U4_2.pin11
  N39: U4.pin14, U4_2.pin14
  N40: U4.pin17, U4_2.pin17
  N41: U4.pin20, U4_2.pin20
  N42: U4.pin23, U4_2.pin23
