# Fritzing sketch Breadboard (saved by Fritzing 0.9.0b)
breadboards: 1

parts:
  U1 = atmega328 [package=dip]
  R1 = Resistor [tolerance=±5% resistance=220 package=THT]
  LED1 = LED - 5mm [color="Green (570nm)" package="5 mm [THT]"]
  S1 = Pushbutton [package="[THT]"]
  R2 = Resistor [tolerance=±5% resistance=10k package=THT]
  C1 = Electrolytic Capacitor [capacitance=10µF package="100 mil [THT, electrolytic]"]

nets:
  N1: U1.RESET, S1.Pin_1, S1.Pin_2, R2.Pin_0
  N2: R1.Pin_0, R2.Pin_1, C1.+
  N3: R1.Pin_1, LED1.anode
  N4: LED1.cathode, S1.Pin_3, S1.Pin_4, C1.-
