# Fritzing sketch nplBreadboard (saved by Fritzing 0.9.0b)
breadboards: 1

parts:
  V1 = DC Power [voltage=5]  # not connected
  U2 = atmega328 [package=dip]
  R4 = Resistor [tolerance=±5% resistance=220 package=THT]
  R5 = Resistor [tolerance=±5% resistance=220 package=THT]
  S4 = Pushbutton [package="[SMD]"]
  R6 = Resistor [tolerance=±5% resistance=10k package=THT]
  LED3 = LED - 5mm [color="Red (633nm)" package="5 mm [THT]"]
  C4 = Electrolytic Capacitor [capacitance=10µF package="100 mil [THT, electrolytic]"]
  XTAL2 = Crystal [frequency="16 Mhz" package=THT]
  LED4 = LED - 5mm [color="Yellow (595nm)" package="5 mm [THT]"]
  C5 = Ceramic Capacitor [capacitance="100 nF" package="1206 [SMD, multilayer]"]
  C6 = Ceramic Capacitor [capacitance="100 nF" package="1206 [SMD, multilayer]"]
  U3 = mystery part, 5 pins [chip_label=SYM-RFT-60]
  Part1 = FTDI Basic Programmer

nets:
  N1: U2.RESET, S4.Pin_1, S4.Pin_2, R6.Pin_0
  N2: U2.D0_(RX), Part1.TXO
  N3: U2.D1_(TX), Part1.RXI
  N4: U2.D2, U2.D3_(PWM), U3.pin4
  N5: U2.VCC, U2.AVCC, R4.Pin_1, R6.Pin_1, C4.+, U3.pin5, Part1.POWER
  GND: U2.GND, S4.Pin_3, S4.Pin_4, LED3.cathode, C4.-, LED4.cathode, C5.1, C6.0, U3.pin2, U3.pin3, Part1.GND
  N6: U2.XLAT1, XTAL2.pin_0, C6.1
  N7: U2.XLAT2, XTAL2.pin_1, C5.0
  N8: U2.D13, R5.Pin_0
  N9: R4.Pin_0, LED3.anode
  N10: R5.Pin_1, LED4.anode
